// Logisim project CPU Components.circ as structural Verilog: 5 circuits, main circuit D-Register
// D
module D_Register (
  input  [15:0] in,
  input  load,
  output [15:0] out
);

  wire clock_1_out;

  Register #(.width(16)) Register (.D(in), .en(load), .Q(out), .clk(clock_1_out));  // open: clr
  Clock clock_1 (.out(clock_1_out));
endmodule

// A
module A_Register (
  input  [15:0] in,
  input  load,
  output [15:0] out
);

  wire clock_1_out;

  Register #(.width(16)) Register (.D(in), .en(load), .Q(out), .clk(clock_1_out));  // open: clr
  Clock clock_1 (.out(clock_1_out));
endmodule

module PC (
  input  load,
  input  [15:0] in,
  input  inc,
  input  reset,
  output [15:0] out
);

  wire clock_1_out;

  Counter #(.width(16), .max('hffff)) PC (
    .load(load), .D(in), .count(inc), .Q(out), .clk(clock_1_out), .clr(reset));  // open: carry
  Clock clock_1 (.out(clock_1_out));
endmodule

// JMP
module Jump_Logic (
  input  ng,
  input  zr,
  input  j1,
  input  j2,
  input  j3,
  input  aOrC,
  output loadPC,
  output inc
);

  wire and_1_out, and_2_out, and_3_out, not_1_out, or_1_out, or_2_out, or_3_out;

  and and_1 (and_1_out, j2, ng);
  and and_2 (and_2_out, j1, zr);
  or or_1 (or_1_out, zr, ng);
  or or_2 (or_2_out, and_2_out, and_1_out);
  not not_1 (not_1_out, or_1_out);
  and and_3 (and_3_out, not_1_out, j3);
  or or_3 (or_3_out, or_2_out, and_3_out);
  and and_4 (loadPC, or_3_out, aOrC);
  not not_2 (inc, loadPC);

  // Notes on the sheet:
  //   JLT
  //   JEQ
  //   checkGT
  //   JLE
  //   GT
  //   JGT
  //   JMP
endmodule

// Decode Instruction
module Decode (
  input  [15:0] instruction,
  output zx,
  output nx,
  output zy,
  output n,
  output f,
  output no,
  output j1,
  output j2,
  output j3,
  output aOrC,
  output aOrC_2,
  output loadD,
  output loadA,
  output writeM,
  output aOrM
);

  wire not_1_out;

  and and_1 (loadD, instruction[15], instruction[4]);
  not not_1 (not_1_out, instruction[15]);
  or or_1 (loadA, not_1_out, instruction[5]);
  and and_2 (writeM, instruction[15], instruction[3]);

  assign aOrC = instruction[15];
  assign aOrC_2 = instruction[15];
  assign aOrM = instruction[12];
  assign f = instruction[7];
  assign j1 = instruction[2];
  assign j2 = instruction[1];
  assign j3 = instruction[0];
  assign n = instruction[8];
  assign no = instruction[6];
  assign nx = instruction[10];
  assign zx = instruction[11];
  assign zy = instruction[9];

  // Notes on the sheet:
  //   [15]
  //   notI15
  //   [4]
  //   [3]
  //   [5]
  //   [12]
  //   [11, 10, 9, 8, 7, 6]
  //   [1]
  //   [2]
  //   [15]
  //   [0]
endmodule
