// Logisim project CS2 Logisim Portfolio.circ as structural Verilog: 32 circuits, main circuit Not
module Not (
  input  in,
  output out
);

  nand nand_1 (out, in, in);
endmodule

module And (
  input  a,
  input  b,
  output out
);

  wire nand_1_out;

  nand nand_1 (nand_1_out, a, b);
  not not_1 (out, nand_1_out);

  // Notes on the sheet:
  //   c
endmodule

module Or (
  input  a,
  input  b,
  output out
);

  wire not_1_out, not_2_out;

  not not_1 (not_1_out, a);
  not not_2 (not_2_out, b);
  nand nand_1 (out, not_1_out, not_2_out);

  // Notes on the sheet:
  //   notA
  //   notB
endmodule

module Xor (
  input  a,
  input  b,
  output out
);

  wire nand_1_out, or_1_out;

  or or_1 (or_1_out, a, b);
  nand nand_1 (nand_1_out, b, a);
  and and_1 (out, or_1_out, nand_1_out);

  // Notes on the sheet:
  //   orOut
  //   nandOut
endmodule

module Mux (
  input  a,
  input  sel,
  input  b,
  input  a_2,
  input  sel_2,
  input  b_2,
  output out,
  output out_2
);

  wire and_1_out, and_2_out, nand_1_out, nand_2_out, not_1_out, not_2_out;

  not not_1 (not_1_out, sel);
  not not_2 (not_2_out, sel_2);
  and and_1 (and_1_out, a, not_1_out);
  and and_2 (and_2_out, sel, b);
  nand nand_1 (nand_1_out, a_2, not_2_out);
  nand nand_2 (nand_2_out, sel_2, b_2);
  or or_1 (out, and_1_out, and_2_out);
  nand nand_3 (out_2, nand_1_out, nand_2_out);

  // Notes on the sheet:
  //   Alternative
  //   notSel
  //   notSel
  //   aOut
  //   bOut
  //   aOut
  //   bOut
endmodule

module DMux (
  input  in,
  input  sel,
  input  in_2,
  input  sel_2,
  output a,
  output b,
  output a_2,
  output b_2
);

  wire not_1_out;

  not not_1 (not_1_out, sel);
  and and_1 (b_2, in_2, sel_2);
  and and_2 (a, in, not_1_out);
  and and_3 (b, sel, in);
  xor Xor (a_2, in_2, b_2);

  // Notes on the sheet:
  //   notSel
  //   Alternative
  //   a1
endmodule

module Not16 (
  input  [15:0] in,
  output [15:0] out
);

  not not_1 (out[0], in[0]);
  not not_2 (out[1], in[1]);
  not not_3 (out[2], in[2]);
  not not_4 (out[3], in[3]);
  not not_5 (out[4], in[4]);
  not not_6 (out[5], in[5]);
  not not_7 (out[6], in[6]);
  not not_8 (out[7], in[7]);
  not not_9 (out[8], in[8]);
  not not_10 (out[9], in[9]);
  not not_11 (out[10], in[10]);
  not not_12 (out[11], in[11]);
  not not_13 (out[12], in[12]);
  not not_14 (out[13], in[13]);
  not not_15 (out[14], in[14]);
  not not_16 (out[15], in[15]);
endmodule

module And16 (
  input  [15:0] a,
  input  [15:0] b,
  output [15:0] out
);

  and and_1 (out[0], a[0], b[0]);
  and and_2 (out[1], a[1], b[1]);
  and and_3 (out[2], a[2], b[2]);
  and and_4 (out[3], a[3], b[3]);
  and and_5 (out[4], a[4], b[4]);
  and and_6 (out[5], a[5], b[5]);
  and and_7 (out[6], a[6], b[6]);
  and and_8 (out[7], a[7], b[7]);
  and and_9 (out[8], a[8], b[8]);
  and and_10 (out[9], a[9], b[9]);
  and and_11 (out[10], a[10], b[10]);
  and and_12 (out[11], a[11], b[11]);
  and and_13 (out[12], a[12], b[12]);
  and and_14 (out[13], a[13], b[13]);
  and and_15 (out[14], a[14], b[14]);
  and and_16 (out[15], a[15], b[15]);
endmodule

module Or16 (
  input  [15:0] a,
  input  [15:0] b,
  output [15:0] out
);

  or or_1 (out[0], a[0], b[0]);
  or or_2 (out[1], a[1], b[1]);
  or or_3 (out[2], a[2], b[2]);
  or or_4 (out[3], a[3], b[3]);
  or or_5 (out[4], a[4], b[4]);
  or or_6 (out[5], a[5], b[5]);
  or or_7 (out[6], a[6], b[6]);
  or or_8 (out[7], a[7], b[7]);
  or or_9 (out[8], a[8], b[8]);
  or or_10 (out[9], a[9], b[9]);
  or or_11 (out[10], a[10], b[10]);
  or or_12 (out[11], a[11], b[11]);
  or or_13 (out[12], a[12], b[12]);
  or or_14 (out[13], a[13], b[13]);
  or or_15 (out[14], a[14], b[14]);
  or or_16 (out[15], a[15], b[15]);
endmodule

module Mux16 (
  input  [15:0] a,
  input  [15:0] b,
  input  sel,
  output [15:0] out
);

  Multiplexer #(.enable("false")) multiplexer_1 (.in0(a[0]), .in1(b[0]), .out(out[0]), .sel(sel));
  Multiplexer #(.enable("false")) multiplexer_2 (.in0(a[1]), .in1(b[1]), .out(out[1]), .sel(sel));
  Multiplexer #(.enable("false")) multiplexer_3 (.in0(a[2]), .in1(b[2]), .out(out[2]), .sel(sel));
  Multiplexer #(.enable("false")) multiplexer_4 (.in0(a[3]), .in1(b[3]), .out(out[3]), .sel(sel));
  Multiplexer #(.enable("false")) multiplexer_5 (.in0(a[4]), .in1(b[4]), .out(out[4]), .sel(sel));
  Multiplexer #(.enable("false")) multiplexer_6 (.in0(a[5]), .in1(b[5]), .out(out[5]), .sel(sel));
  Multiplexer #(.enable("false")) multiplexer_7 (.in0(a[6]), .in1(b[6]), .out(out[6]), .sel(sel));
  Multiplexer #(.enable("false")) multiplexer_8 (.in0(a[7]), .in1(b[7]), .out(out[7]), .sel(sel));
  Multiplexer #(.enable("false")) multiplexer_9 (.in0(a[8]), .in1(b[8]), .out(out[8]), .sel(sel));
  Multiplexer #(.enable("false")) multiplexer_10 (.in0(a[9]), .in1(b[9]), .out(out[9]), .sel(sel));
  Multiplexer #(.enable("false")) multiplexer_11 (.in0(a[10]), .in1(b[10]), .out(out[10]), .sel(sel));
  Multiplexer #(.enable("false")) multiplexer_12 (.in0(a[11]), .in1(b[11]), .out(out[11]), .sel(sel));
  Multiplexer #(.enable("false")) multiplexer_13 (.in0(a[12]), .in1(b[12]), .out(out[12]), .sel(sel));
  Multiplexer #(.enable("false")) multiplexer_14 (.in0(a[13]), .in1(b[13]), .out(out[13]), .sel(sel));
  Multiplexer #(.enable("false")) multiplexer_15 (.in0(a[14]), .in1(b[14]), .out(out[14]), .sel(sel));
  Multiplexer #(.enable("false")) multiplexer_16 (.in0(a[15]), .in1(b[15]), .out(out[15]), .sel(sel));
endmodule

module Or8Way (
  input  [7:0] in,
  output out
);

  wire or_1_out, or_2_out, or_3_out, or_4_out, or_5_out, or_6_out;

  or or_1 (or_1_out, in[0], in[1]);
  or or_2 (or_2_out, in[2], in[3]);
  or or_3 (or_3_out, in[4], in[5]);
  or or_4 (or_4_out, in[6], in[7]);
  or or_5 (or_5_out, or_1_out, or_2_out);
  or or_6 (or_6_out, or_3_out, or_4_out);
  or or_7 (out, or_5_out, or_6_out);

  // Notes on the sheet:
  //   a
  //   b
  //   c
  //   d
  //   x
  //   y
endmodule

module Mux4Way16 (
  input  [15:0] a,
  input  [15:0] b,
  input  [15:0] c,
  input  [15:0] d,
  input  [1:0] sel_0,
  output [15:0] out
);

  wire [15:0] multiplexer_1_out, multiplexer_2_out;

  Multiplexer #(.width(16), .enable("false")) multiplexer_1 (.in0(a), .in1(b), .out(multiplexer_1_out), .sel(sel_0[0]));
  Multiplexer #(.width(16), .enable("false")) multiplexer_2 (.in0(c), .in1(d), .out(multiplexer_2_out), .sel(sel_0[0]));
  Multiplexer #(.width(16), .enable("false")) multiplexer_3 (
    .in0(multiplexer_1_out), .in1(multiplexer_2_out), .out(out), .sel(sel_0[1]));

  // Notes on the sheet:
  //   ab
  //   cd
  //   sel[1]
endmodule

module Mux8Way16 (
  input  [15:0] a,
  input  [15:0] b,
  input  [15:0] c,
  input  [15:0] d,
  input  [15:0] e,
  input  [15:0] f,
  input  [15:0] g,
  input  [15:0] h,
  input  [2:0] sel_0__1,
  output [15:0] out
);

  wire [15:0] multiplexer_1_out, multiplexer_2_out;

  Multiplexer #(.select(2), .width(16), .enable("false")) multiplexer_1 (
    .in0(a), .in1(b), .in2(c), .in3(d), .out(multiplexer_1_out), .sel(sel_0__1[1:0]));
  Multiplexer #(.select(2), .width(16), .enable("false")) multiplexer_2 (
    .in0(e), .in1(f), .in2(g), .in3(h), .out(multiplexer_2_out), .sel(sel_0__1[1:0]));
  Multiplexer #(.width(16), .enable("false")) multiplexer_3 (
    .in0(multiplexer_1_out), .in1(multiplexer_2_out), .out(out), .sel(sel_0__1[2]));

  // Notes on the sheet:
  //   abcd
  //   efgh
  //   sel[2]
endmodule

module DMux4Way (
  input  in,
  input  sel_0,
  input  sel_1,
  output a,
  output b,
  output c,
  output d
);

  wire demultiplexer_1_out0, demultiplexer_1_out1;

  Demultiplexer #(.enable("false")) demultiplexer_1 (
    .out0(demultiplexer_1_out0), .out1(demultiplexer_1_out1), .in(in), .sel(sel_1));
  Demultiplexer #(.enable("false")) demultiplexer_2 (.out0(a), .out1(b), .in(demultiplexer_1_out0), .sel(sel_0));
  Demultiplexer #(.enable("false")) demultiplexer_3 (.out0(c), .out1(d), .in(demultiplexer_1_out1), .sel(sel_0));

  // Notes on the sheet:
  //   ab
  //   cd
endmodule

module DMux8Way (
  input  in,
  input  [1:0] sel_0__1,
  input  sel_2,
  output a,
  output b,
  output c,
  output d,
  output e,
  output f,
  output g,
  output h
);

  wire demultiplexer_1_out0, demultiplexer_1_out1;

  Demultiplexer #(.enable("false")) demultiplexer_1 (
    .out0(demultiplexer_1_out0), .out1(demultiplexer_1_out1), .in(in), .sel(sel_2));
  Demultiplexer #(.select(2), .enable("false")) demultiplexer_2 (
    .out0(a), .out1(b), .out2(c), .out3(d), .in(demultiplexer_1_out0), .sel(sel_0__1));
  Demultiplexer #(.select(2), .enable("false")) demultiplexer_3 (
    .out0(e), .out1(f), .out2(g), .out3(h), .in(demultiplexer_1_out1), .sel(sel_0__1));

  // Notes on the sheet:
  //   abcd
  //   efgh
endmodule

module HalfAdder (
  input  a,
  input  b,
  output sum,
  output carry
);

  xor xor_1 (sum, a, b);
  and and_1 (carry, b, a);
endmodule

module FullAdder (
  input  a,
  input  b,
  input  c,
  output sum,
  output carry
);

  wire adder_1_cout, adder_1_out, adder_2_cout;

  Adder #(.width(1)) adder_1 (.a(a), .b(b), .out(adder_1_out), .cout(adder_1_cout));  // open: cin
  Adder #(.width(1)) adder_2 (.a(adder_1_out), .b(c), .out(sum), .cout(adder_2_cout));  // open: cin
  or or_1 (carry, adder_2_cout, adder_1_cout);

  // Notes on the sheet:
  //   sumAB
  //   c2
  //   c1
endmodule

module Add16 (
  input  [15:0] a,
  input  [15:0] b,
  output [15:0] out
);

  wire adder_1_cout, adder_2_cout, adder_3_cout, adder_4_cout, adder_5_cout, adder_6_cout, adder_7_cout,
       adder_8_cout, adder_9_cout, adder_10_cout, adder_11_cout, adder_12_cout, adder_13_cout, adder_14_cout,
       adder_15_cout;

  Adder #(.width(1)) adder_1 (.a(a[0]), .b(b[0]), .out(out[0]), .cout(adder_1_cout));  // open: cin
  Adder #(.width(1)) adder_2 (.a(a[1]), .b(b[1]), .out(out[1]), .cin(adder_1_cout), .cout(adder_2_cout));
  Adder #(.width(1)) adder_3 (.a(a[2]), .b(b[2]), .out(out[2]), .cin(adder_2_cout), .cout(adder_3_cout));
  Adder #(.width(1)) adder_4 (.a(a[3]), .b(b[3]), .out(out[3]), .cin(adder_3_cout), .cout(adder_4_cout));
  Adder #(.width(1)) adder_5 (.a(a[4]), .b(b[4]), .out(out[4]), .cin(adder_4_cout), .cout(adder_5_cout));
  Adder #(.width(1)) adder_6 (.a(a[5]), .b(b[5]), .out(out[5]), .cin(adder_5_cout), .cout(adder_6_cout));
  Adder #(.width(1)) adder_7 (.a(a[6]), .b(b[6]), .out(out[6]), .cin(adder_6_cout), .cout(adder_7_cout));
  Adder #(.width(1)) adder_8 (.a(a[7]), .b(b[7]), .out(out[7]), .cin(adder_7_cout), .cout(adder_8_cout));
  Adder #(.width(1)) adder_9 (.a(a[8]), .b(b[8]), .out(out[8]), .cin(adder_8_cout), .cout(adder_9_cout));
  Adder #(.width(1)) adder_10 (.a(a[9]), .b(b[9]), .out(out[9]), .cin(adder_9_cout), .cout(adder_10_cout));
  Adder #(.width(1)) adder_11 (.a(a[10]), .b(b[10]), .out(out[10]), .cin(adder_10_cout), .cout(adder_11_cout));
  Adder #(.width(1)) adder_12 (.a(a[11]), .b(b[11]), .out(out[11]), .cin(adder_11_cout), .cout(adder_12_cout));
  Adder #(.width(1)) adder_13 (.a(a[12]), .b(b[12]), .out(out[12]), .cin(adder_12_cout), .cout(adder_13_cout));
  Adder #(.width(1)) adder_14 (.a(a[13]), .b(b[13]), .out(out[13]), .cin(adder_13_cout), .cout(adder_14_cout));
  Adder #(.width(1)) adder_15 (.a(a[14]), .b(b[14]), .out(out[14]), .cin(adder_14_cout), .cout(adder_15_cout));
  Adder #(.width(1)) adder_16 (.a(a[15]), .b(b[15]), .out(out[15]), .cin(adder_15_cout));  // open: cout

  // Notes on the sheet:
  //   c0
  //   c1
  //   c2
  //   c3
  //   c4
  //   c5
  //   c6
  //   c7
  //   c8
  //   c9
  //   c10
  //   c11
  //   c12
  //   c13
  //   c14
endmodule

module Inc16 (
  input  [15:0] a,
  output [15:0] out
);

  Adder #(.width(16)) adder_1 (.a(a), .b(16'h1), .out(out));  // open: cin, cout

  // Notes on the sheet:
  //   b[0] = true
endmodule

module ALU (
  input  [15:0] x,
  input  zx,
  input  nx,
  input  zy,
  input  ny,
  input  f,
  input  no,
  input  [15:0] y,
  output [15:0] out,
  output zr,
  output ng
);

  wire or8way_1_out, or8way_2_out, or_1_out;
  wire [15:0] adder_1_out, and_1_out, multiplexer_1_out, multiplexer_2_out, multiplexer_3_out,
       multiplexer_4_out, multiplexer_5_out, not_1_out, not_2_out, not_3_out;

  Multiplexer #(.width(16), .enable("false")) multiplexer_1 (
    .in0(x), .in1({16{1'b0}}), .out(multiplexer_1_out), .sel(zx));
  Multiplexer #(.width(16), .enable("false")) multiplexer_2 (
    .in0(y), .in1({16{1'b0}}), .out(multiplexer_2_out), .sel(zy));
  assign not_1_out = ~multiplexer_1_out;  // NOT_Gate not_1, 16 bits wide
  assign not_2_out = ~multiplexer_2_out;  // NOT_Gate not_2, 16 bits wide
  Multiplexer #(.width(16), .enable("false")) multiplexer_3 (
    .in0(multiplexer_1_out), .in1(not_1_out), .out(multiplexer_3_out), .sel(nx));
  Multiplexer #(.width(16), .enable("false")) multiplexer_4 (
    .in0(multiplexer_2_out), .in1(not_2_out), .out(multiplexer_4_out), .sel(ny));
  assign and_1_out = multiplexer_3_out & multiplexer_4_out;  // AND_Gate and_1, 16 bits wide
  Adder #(.width(16)) adder_1 (.a(multiplexer_3_out), .b(multiplexer_4_out), .out(adder_1_out));  // open: cin, cout
  Multiplexer #(.width(16), .enable("false")) multiplexer_5 (
    .in0(and_1_out), .in1(adder_1_out), .out(multiplexer_5_out), .sel(f));
  assign not_3_out = ~multiplexer_5_out;  // NOT_Gate not_3, 16 bits wide
  Multiplexer #(.width(16), .enable("false")) multiplexer_6 (
    .in0(multiplexer_5_out), .in1(not_3_out), .out({ng, out[14:0]}), .sel(no));
  Or8Way or8way_1 (.in(out[7:0]), .out(or8way_1_out));
  Or8Way or8way_2 (.in({ng, out[14:8]}), .out(or8way_2_out));
  not not_4 (zr, or_1_out);
  or or_1 (or_1_out, or8way_1_out, or8way_2_out);

  assign out[15] = ng;

  // Notes on the sheet:
  //   b = false
  //   b = false
  //   x1
  //   y1
  //   notY
  //   x2
  //   notX
  //   y2
  //   andXY
  //   addXY
  //   fXY
  //   notFXY
  //   out[0..7] = outA
  //   out[8..15] = outB
  //   orA
  //   orB
  //   out[15]
  //   orC
endmodule

module Bit (
  input  in,
  input  load,
  output out
);

  wire Clock__built_in_out, multiplexer_1_out;

  Multiplexer #(.enable("false")) multiplexer_1 (.in0(out), .in1(in), .out(multiplexer_1_out), .sel(load));
  Clock Clock__built_in (.out(Clock__built_in_out));
  D_Flip_Flop d_ff_1 (.clk(Clock__built_in_out), .D(multiplexer_1_out), .Q(out));  // open: Qn, preset, en, reset

  // Notes on the sheet:
  //   dffOut
  //   DFF (Data Flip-Flop)
endmodule

module Register (
  input  [15:0] in,
  input  load,
  output [15:0] out
);

  wire clock_1_out;

  Clock clock_1 (.out(clock_1_out));
  D_Flip_Flop d_ff_1 (.clk(clock_1_out), .D(in[0]), .Q(out[0]), .en(load));  // open: Qn, preset, reset
  D_Flip_Flop d_ff_2 (.clk(clock_1_out), .D(in[1]), .Q(out[1]), .en(load));  // open: Qn, preset, reset
  D_Flip_Flop d_ff_3 (.clk(clock_1_out), .D(in[2]), .Q(out[2]), .en(load));  // open: Qn, preset, reset
  D_Flip_Flop d_ff_4 (.clk(clock_1_out), .D(in[3]), .Q(out[3]), .en(load));  // open: Qn, preset, reset
  D_Flip_Flop d_ff_5 (.clk(clock_1_out), .D(in[4]), .Q(out[4]), .en(load));  // open: Qn, preset, reset
  D_Flip_Flop d_ff_6 (.clk(clock_1_out), .D(in[5]), .Q(out[5]), .en(load));  // open: Qn, preset, reset
  D_Flip_Flop d_ff_7 (.clk(clock_1_out), .D(in[6]), .Q(out[6]), .en(load));  // open: Qn, preset, reset
  D_Flip_Flop d_ff_8 (.clk(clock_1_out), .D(in[7]), .Q(out[7]), .en(load));  // open: Qn, preset, reset
  D_Flip_Flop d_ff_9 (.clk(clock_1_out), .D(in[8]), .Q(out[8]), .en(load));  // open: Qn, preset, reset
  D_Flip_Flop d_ff_10 (.clk(clock_1_out), .D(in[9]), .Q(out[9]), .en(load));  // open: Qn, preset, reset
  D_Flip_Flop d_ff_11 (.clk(clock_1_out), .D(in[10]), .Q(out[10]), .en(load));  // open: Qn, preset, reset
  D_Flip_Flop d_ff_12 (.clk(clock_1_out), .D(in[11]), .Q(out[11]), .en(load));  // open: Qn, preset, reset
  D_Flip_Flop d_ff_13 (.clk(clock_1_out), .D(in[12]), .Q(out[12]), .en(load));  // open: Qn, preset, reset
  D_Flip_Flop d_ff_14 (.clk(clock_1_out), .D(in[13]), .Q(out[13]), .en(load));  // open: Qn, preset, reset
  D_Flip_Flop d_ff_15 (.clk(clock_1_out), .D(in[14]), .Q(out[14]), .en(load));  // open: Qn, preset, reset
  D_Flip_Flop d_ff_16 (.clk(clock_1_out), .D(in[15]), .Q(out[15]), .en(load));  // open: Qn, preset, reset
endmodule

module RAM8 (
  input  [15:0] in,
  input  load,
  input  [2:0] address,
  output [15:0] out
);

  wire clock_1_out, demultiplexer_1_out0, demultiplexer_1_out1, demultiplexer_1_out2, demultiplexer_1_out3,
       demultiplexer_1_out4, demultiplexer_1_out5, demultiplexer_1_out6, demultiplexer_1_out7;
  wire [15:0] register_1_q, register_2_q, register_3_q, register_4_q, register_5_q, register_6_q,
       register_7_q, register_8_q;

  Demultiplexer #(.select(3), .enable("false")) demultiplexer_1 (
    .out0(demultiplexer_1_out0), .out1(demultiplexer_1_out1), .out2(demultiplexer_1_out2),
    .out3(demultiplexer_1_out3), .out4(demultiplexer_1_out4), .out5(demultiplexer_1_out5),
    .out6(demultiplexer_1_out6), .out7(demultiplexer_1_out7), .in(load), .sel(address));
  Register_part #(.width(16)) register_1 (
    .D(in), .en(demultiplexer_1_out0), .Q(register_1_q), .clk(clock_1_out));  // open: clr
  Register_part #(.width(16)) register_2 (
    .D(in), .en(demultiplexer_1_out1), .Q(register_2_q), .clk(clock_1_out));  // open: clr
  Register_part #(.width(16)) register_3 (
    .D(in), .en(demultiplexer_1_out2), .Q(register_3_q), .clk(clock_1_out));  // open: clr
  Register_part #(.width(16)) register_4 (
    .D(in), .en(demultiplexer_1_out3), .Q(register_4_q), .clk(clock_1_out));  // open: clr
  Register_part #(.width(16)) register_5 (
    .D(in), .en(demultiplexer_1_out4), .Q(register_5_q), .clk(clock_1_out));  // open: clr
  Register_part #(.width(16)) register_6 (
    .D(in), .en(demultiplexer_1_out5), .Q(register_6_q), .clk(clock_1_out));  // open: clr
  Register_part #(.width(16)) register_7 (
    .D(in), .en(demultiplexer_1_out6), .Q(register_7_q), .clk(clock_1_out));  // open: clr
  Register_part #(.width(16)) register_8 (
    .D(in), .en(demultiplexer_1_out7), .Q(register_8_q), .clk(clock_1_out));  // open: clr
  Clock clock_1 (.out(clock_1_out));
  Multiplexer #(.select(3), .width(16), .enable("false")) multiplexer_1 (
    .in0(register_1_q), .in1(register_2_q), .in2(register_3_q), .in3(register_4_q), .in4(register_5_q),
    .in5(register_6_q), .in6(register_7_q), .in7(register_8_q), .out(out), .sel(address));

  // Notes on the sheet:
  //   load0
  //   load1
  //   load2
  //   load3
  //   load4
  //   load5
  //   load6
  //   load7
  //   out0
  //   out1
  //   out2
  //   out3
  //   out4
  //   out5
  //   out6
  //   out7
endmodule

module RAM64 (
  input  [15:0] in,
  input  load,
  input  [5:0] address,
  output [15:0] out
);

  wire demultiplexer_1_out0, demultiplexer_1_out1, demultiplexer_1_out2, demultiplexer_1_out3,
       demultiplexer_1_out4, demultiplexer_1_out5, demultiplexer_1_out6, demultiplexer_1_out7;
  wire [15:0] ram8_1_out, ram8_2_out, ram8_3_out, ram8_4_out, ram8_5_out, ram8_6_out, ram8_7_out, ram8_8_out;

  Demultiplexer #(.select(3), .enable("false")) demultiplexer_1 (
    .out0(demultiplexer_1_out0), .out1(demultiplexer_1_out1), .out2(demultiplexer_1_out2),
    .out3(demultiplexer_1_out3), .out4(demultiplexer_1_out4), .out5(demultiplexer_1_out5),
    .out6(demultiplexer_1_out6), .out7(demultiplexer_1_out7), .in(load), .sel(address[5:3]));
  RAM8 ram8_1 (.in(in), .load(demultiplexer_1_out0), .out(ram8_1_out), .address(address[2:0]));
  RAM8 ram8_2 (.in(in), .load(demultiplexer_1_out1), .out(ram8_2_out), .address(address[2:0]));
  RAM8 ram8_3 (.in(in), .load(demultiplexer_1_out2), .out(ram8_3_out), .address(address[2:0]));
  RAM8 ram8_4 (.in(in), .load(demultiplexer_1_out3), .out(ram8_4_out), .address(address[2:0]));
  RAM8 ram8_5 (.in(in), .load(demultiplexer_1_out4), .out(ram8_5_out), .address(address[2:0]));
  RAM8 ram8_6 (.in(in), .load(demultiplexer_1_out5), .out(ram8_6_out), .address(address[2:0]));
  RAM8 ram8_7 (.in(in), .load(demultiplexer_1_out6), .out(ram8_7_out), .address(address[2:0]));
  RAM8 ram8_8 (.in(in), .load(demultiplexer_1_out7), .out(ram8_8_out), .address(address[2:0]));
  Multiplexer #(.select(3), .width(16), .enable("false")) multiplexer_1 (
    .in0(ram8_1_out), .in1(ram8_2_out), .in2(ram8_3_out), .in3(ram8_4_out), .in4(ram8_5_out),
    .in5(ram8_6_out), .in6(ram8_7_out), .in7(ram8_8_out), .out(out), .sel(address[5:3]));

  // Notes on the sheet:
  //   load0
  //   load1
  //   load2
  //   load3
  //   load4
  //   load5
  //   load6
  //   load7
  //   address[0..2]
  //   address[3..5]
  //   out0
  //   out1
  //   out2
  //   out3
  //   out4
  //   out5
  //   out6
  //   out7
endmodule

module RAM512 (
  input  [15:0] in,
  input  load,
  input  [8:0] address,
  output [15:0] out
);

  wire demultiplexer_1_out0, demultiplexer_1_out1, demultiplexer_1_out2, demultiplexer_1_out3,
       demultiplexer_1_out4, demultiplexer_1_out5, demultiplexer_1_out6, demultiplexer_1_out7;
  wire [15:0] ram64_1_out, ram64_2_out, ram64_3_out, ram64_4_out, ram64_5_out, ram64_6_out, ram64_7_out,
       ram64_8_out;

  Demultiplexer #(.select(3), .enable("false")) demultiplexer_1 (
    .out0(demultiplexer_1_out0), .out1(demultiplexer_1_out1), .out2(demultiplexer_1_out2),
    .out3(demultiplexer_1_out3), .out4(demultiplexer_1_out4), .out5(demultiplexer_1_out5),
    .out6(demultiplexer_1_out6), .out7(demultiplexer_1_out7), .in(load), .sel(address[8:6]));
  RAM64 ram64_1 (.in(in), .load(demultiplexer_1_out0), .out(ram64_1_out), .address(address[5:0]));
  RAM64 ram64_2 (.in(in), .load(demultiplexer_1_out1), .out(ram64_2_out), .address(address[5:0]));
  RAM64 ram64_3 (.in(in), .load(demultiplexer_1_out2), .out(ram64_3_out), .address(address[5:0]));
  RAM64 ram64_4 (.in(in), .load(demultiplexer_1_out3), .out(ram64_4_out), .address(address[5:0]));
  RAM64 ram64_5 (.in(in), .load(demultiplexer_1_out4), .out(ram64_5_out), .address(address[5:0]));
  RAM64 ram64_6 (.in(in), .load(demultiplexer_1_out5), .out(ram64_6_out), .address(address[5:0]));
  RAM64 ram64_7 (.in(in), .load(demultiplexer_1_out6), .out(ram64_7_out), .address(address[5:0]));
  RAM64 ram64_8 (.in(in), .load(demultiplexer_1_out7), .out(ram64_8_out), .address(address[5:0]));
  Multiplexer #(.select(3), .width(16), .enable("false")) multiplexer_1 (
    .in0(ram64_1_out), .in1(ram64_2_out), .in2(ram64_3_out), .in3(ram64_4_out), .in4(ram64_5_out),
    .in5(ram64_6_out), .in6(ram64_7_out), .in7(ram64_8_out), .out(out), .sel(address[8:6]));

  // Notes on the sheet:
  //   load0
  //   load1
  //   load2
  //   load3
  //   load4
  //   load5
  //   load6
  //   load7
  //   address[0..5]
  //   address[6..8]
  //   out0
  //   out1
  //   out2
  //   out3
  //   out4
  //   out5
  //   out6
  //   out7
endmodule

module RAM4K (
  input  [15:0] in,
  input  load,
  input  [11:0] address,
  output [15:0] out
);

  wire demultiplexer_1_out0, demultiplexer_1_out1, demultiplexer_1_out2, demultiplexer_1_out3,
       demultiplexer_1_out4, demultiplexer_1_out5, demultiplexer_1_out6, demultiplexer_1_out7;
  wire [15:0] ram512_1_out, ram512_2_out, ram512_3_out, ram512_4_out, ram512_5_out, ram512_6_out,
       ram512_7_out, ram512_8_out;

  Demultiplexer #(.select(3), .enable("false")) demultiplexer_1 (
    .out0(demultiplexer_1_out0), .out1(demultiplexer_1_out1), .out2(demultiplexer_1_out2),
    .out3(demultiplexer_1_out3), .out4(demultiplexer_1_out4), .out5(demultiplexer_1_out5),
    .out6(demultiplexer_1_out6), .out7(demultiplexer_1_out7), .in(load), .sel(address[11:9]));
  RAM512 ram512_1 (.in(in), .load(demultiplexer_1_out0), .address(address[8:0]), .out(ram512_1_out));
  RAM512 ram512_2 (.in(in), .load(demultiplexer_1_out1), .address(address[8:0]), .out(ram512_2_out));
  RAM512 ram512_3 (.in(in), .load(demultiplexer_1_out2), .address(address[8:0]), .out(ram512_3_out));
  RAM512 ram512_4 (.in(in), .load(demultiplexer_1_out3), .address(address[8:0]), .out(ram512_4_out));
  RAM512 ram512_5 (.in(in), .load(demultiplexer_1_out4), .address(address[8:0]), .out(ram512_5_out));
  RAM512 ram512_6 (.in(in), .load(demultiplexer_1_out5), .address(address[8:0]), .out(ram512_6_out));
  RAM512 ram512_7 (.in(in), .load(demultiplexer_1_out6), .address(address[8:0]), .out(ram512_7_out));
  RAM512 ram512_8 (.in(in), .load(demultiplexer_1_out7), .address(address[8:0]), .out(ram512_8_out));
  Multiplexer #(.select(3), .width(16), .enable("false")) multiplexer_1 (
    .in0(ram512_1_out), .in1(ram512_2_out), .in2(ram512_3_out), .in3(ram512_4_out), .in4(ram512_5_out),
    .in5(ram512_6_out), .in6(ram512_7_out), .in7(ram512_8_out), .out(out), .sel(address[11:9]));

  // Notes on the sheet:
  //   load0
  //   load1
  //   load2
  //   load3
  //   load4
  //   load5
  //   load6
  //   load7
  //   address[0..8]
  //   address[9..11]
  //   out0
  //   out1
  //   out2
  //   out3
  //   out4
  //   out5
  //   out6
  //   out7
endmodule

module RAM16K (
  input  [15:0] in,
  input  load,
  input  [13:0] address,
  output [15:0] out
);

  wire demultiplexer_1_out0, demultiplexer_1_out1, demultiplexer_1_out2, demultiplexer_1_out3;
  wire [15:0] ram4k_1_out, ram4k_2_out, ram4k_3_out, ram4k_4_out;

  Demultiplexer #(.select(2), .enable("false")) demultiplexer_1 (
    .out0(demultiplexer_1_out0), .out1(demultiplexer_1_out1), .out2(demultiplexer_1_out2),
    .out3(demultiplexer_1_out3), .in(load), .sel(address[13:12]));
  RAM4K ram4k_1 (.in(in), .load(demultiplexer_1_out0), .address(address[11:0]), .out(ram4k_1_out));
  RAM4K ram4k_2 (.in(in), .load(demultiplexer_1_out1), .address(address[11:0]), .out(ram4k_2_out));
  RAM4K ram4k_3 (.in(in), .load(demultiplexer_1_out2), .address(address[11:0]), .out(ram4k_3_out));
  RAM4K ram4k_4 (.in(in), .load(demultiplexer_1_out3), .address(address[11:0]), .out(ram4k_4_out));
  Multiplexer #(.select(2), .width(16), .enable("false")) multiplexer_1 (
    .in0(ram4k_1_out), .in1(ram4k_2_out), .in2(ram4k_3_out), .in3(ram4k_4_out), .out(out),
    .sel(address[13:12]));

  // Notes on the sheet:
  //   load0
  //   load1
  //   load2
  //   load3
  //   address[0..11]
  //   address[11..12]
  //   out0
  //   out1
  //   out2
  //   out3
endmodule

module PC (
  input  [15:0] in,
  input  reset,
  input  load,
  input  inc,
  input  [15:0] in_2,
  input  sel_2____reset,
  input  sel_1____inc,
  input  sel_0____load,
  output [15:0] out,
  output [15:0] out_2
);

  wire clock_1_out, clock_2_out, or_1_out, or_2_out;
  wire [15:0] inc16_1_out, inc16_2_out, multiplexer_1_out, multiplexer_2_out, multiplexer_3_out;

  Inc16 inc16_1 (.a(out), .out(inc16_1_out));
  Inc16 inc16_2 (.a(out_2), .out(inc16_2_out));
  Multiplexer #(.width(16), .enable("false")) multiplexer_1 (
    .in0(inc16_1_out), .in1(in), .out(multiplexer_1_out), .sel(load));
  or or_1 (or_1_out, load, inc);
  Multiplexer #(.select(3), .width(16), .enable("false")) multiplexer_2 (
    .in0(out_2), .in1(in_2), .in2(inc16_2_out), .in3(in_2), .in4({16{1'b0}}), .in5({16{1'b0}}),
    .in6({16{1'b0}}), .in7({16{1'b0}}), .out(multiplexer_2_out),
    .sel({sel_2____reset, sel_1____inc, sel_0____load}));
  Multiplexer #(.width(16), .enable("false")) multiplexer_3 (
    .in0(multiplexer_1_out), .in1({16{1'b0}}), .out(multiplexer_3_out), .sel(reset));
  or or_2 (or_2_out, reset, or_1_out);
  Register_part #(.width(16)) register_1 (.D(multiplexer_2_out), .en(1'b1), .Q(out_2), .clk(clock_1_out));  // open: clr
  Clock clock_1 (.out(clock_1_out));
  Register_part #(.width(16)) register_2 (
    .D(multiplexer_3_out), .en(or_2_out), .Q(out), .clk(clock_2_out));  // open: clr
  Clock clock_2 (.out(clock_2_out));

  // Notes on the sheet:
  //   incOut
  //   incOut
  //   preData
  //   preLoad
  //   Alternative
  //   data
  //   recurse
  //   data
  //   loadReg
  //   recurse
endmodule

module Screen (
  input  [15:0] in,
  input  load,
  input  [12:0] address,
  output [15:0] out
);

  wire demultiplexer_1_out0, demultiplexer_1_out1;
  wire [15:0] ram4k_1_out, ram4k_2_out;

  Demultiplexer #(.enable("false")) demultiplexer_1 (
    .out0(demultiplexer_1_out0), .out1(demultiplexer_1_out1), .in(load), .sel(address[12]));
  RAM4K ram4k_1 (.in(in), .load(demultiplexer_1_out0), .address(address[11:0]), .out(ram4k_1_out));
  RAM4K ram4k_2 (.in(in), .load(demultiplexer_1_out1), .address(address[11:0]), .out(ram4k_2_out));
  Multiplexer #(.width(16), .enable("false")) multiplexer_1 (
    .in0(ram4k_1_out), .in1(ram4k_2_out), .out(out), .sel(address[12]));

  // Notes on the sheet:
  //   load0
  //   load1
  //   out0
  //   out1
endmodule

module Memory (
  input  [15:0] in,
  input  load,
  input  [14:0] address,
  output [15:0] out
);

  wire clock_1_out, demultiplexer_1_out0, demultiplexer_1_out1;
  wire [6:0] keyboard_1_data;
  wire [15:0] bit_extender_1_out, ram16k_1_out, screen_1_out;

  Demultiplexer #(.enable("false")) demultiplexer_1 (
    .out0(demultiplexer_1_out0), .out1(demultiplexer_1_out1), .in(load), .sel(address[14]));
  RAM16K ram16k_1 (.in(in), .load(demultiplexer_1_out0), .address(address[13:0]), .out(ram16k_1_out));
  Screen screen_1 (.in(in), .load(demultiplexer_1_out1), .address(address[12:0]), .out(screen_1_out));
  Keyboard keyboard_1 (.clk(clock_1_out), .data(keyboard_1_data));  // open: re, clr, avail
  Clock clock_1 (.out(clock_1_out));
  Multiplexer #(.select(2), .width(16), .enable("false")) multiplexer_1 (
    .in0(ram16k_1_out), .in1(ram16k_1_out), .in2(screen_1_out), .in3(bit_extender_1_out), .out(out),
    .sel(address[14:13]));
  assign bit_extender_1_out = {{9{1'b0}}, keyboard_1_data};  // Bit_Extender bit_extender_1

  // Notes on the sheet:
  //   [14]
  //   [0..12]
  //   [0..13]
  //   Keyboard
  //   [13..14]
endmodule

module CPU (
  input  reset,
  input  [15:0] inM,
  input  [15:0] instruction,
  output [15:0] outM,
  output [14:0] addressM,
  output [14:0] pc,
  output writeM
);

  wire alu_1_ng, alu_1_zr, decode_1_aorc, decode_1_aorc_2, decode_1_aorm, decode_1_f, decode_1_j1,
       decode_1_j2, decode_1_j3, decode_1_loada, decode_1_loadd, decode_1_n, decode_1_no, decode_1_nx,
       decode_1_zx, decode_1_zy, jump_logic_1_inc, jump_logic_1_loadpc;
  wire [15:0] d_register_1_out, multiplexer_1_out, multiplexer_2_out;
  wire [15:15] a_register_1_out, pc_1_out;

  Multiplexer #(.width(16), .enable("false")) multiplexer_1 (
    .in0(instruction), .in1(outM), .out(multiplexer_1_out), .sel(decode_1_aorc_2));
  D_Register d_register_1 (.in(outM), .load(decode_1_loadd), .out(d_register_1_out));
  A_Register a_register_1 (.in(multiplexer_1_out), .load(decode_1_loada), .out({a_register_1_out[15], addressM}));
  Multiplexer #(.width(16), .enable("false")) multiplexer_2 (
    .in0({a_register_1_out[15], addressM}), .in1(inM), .out(multiplexer_2_out), .sel(decode_1_aorm));
  Decode decode_1 (
    .aOrC_2(decode_1_aorc_2), .loadD(decode_1_loadd), .loadA(decode_1_loada), .writeM(writeM),
    .aOrM(decode_1_aorm), .zx(decode_1_zx), .nx(decode_1_nx), .zy(decode_1_zy), .n(decode_1_n),
    .f(decode_1_f), .no(decode_1_no), .j1(decode_1_j1), .j2(decode_1_j2), .j3(decode_1_j3),
    .aOrC(decode_1_aorc), .instruction(instruction));
  ALU alu_1 (
    .x(d_register_1_out), .y(multiplexer_2_out), .out(outM), .zr(alu_1_zr), .ng(alu_1_ng), .zy(decode_1_zy),
    .ny(decode_1_n), .zx(decode_1_zx), .nx(decode_1_nx), .f(decode_1_f), .no(decode_1_no));
  CPU_Components_PC pc_1 (
    .load(jump_logic_1_loadpc), .in({a_register_1_out[15], addressM}), .inc(jump_logic_1_inc),
    .out({pc_1_out[15], pc}), .reset(reset));
  Jump_Logic jump_logic_1 (
    .ng(alu_1_zr), .zr(alu_1_ng), .loadPC(jump_logic_1_loadpc), .inc(jump_logic_1_inc), .j3(decode_1_j3),
    .j1(decode_1_j1), .aOrC(decode_1_aorc), .j2(decode_1_j2));

  // Notes on the sheet:
  //   inA
  //   aOrC
  //   loadD
  //   outD
  //   outA
  //   loadA
  //   AM
  //   aOrM
  //   outALU
  //   zr
  //   ng
  //   outA[0..14]
  //   inc
  //   j1
  //   j2
  //   j3
  //   aOrC
  //   loadPC
  //   pc[0..14]
endmodule

module Computer (
  input  reset
);

  wire cpu_1_writem;
  wire [14:0] cpu_1_addressm, cpu_1_pc;
  wire [15:0] cpu_1_outm, memory_1_out, rom_1_data;

  ROM #(.addrWidth(15), .dataWidth(16)) rom_1 (.addr(cpu_1_pc), .data(rom_1_data));  // open: sel
  CPU cpu_1 (
    .writeM(cpu_1_writem), .outM(cpu_1_outm), .addressM(cpu_1_addressm), .pc(cpu_1_pc), .reset(reset),
    .inM(memory_1_out), .instruction(rom_1_data));
  Memory memory_1 (.in(cpu_1_outm), .load(cpu_1_writem), .out(memory_1_out), .address(cpu_1_addressm));

  // Notes on the sheet:
  //   ROM32K
  //   instruction
  //   pc
  //   inM
  //   writeM
  //   outM
  //   addressM
endmodule
