// Logisim project Gas Sensor.circ as structural Verilog: 1 circuit, main circuit main
module main (
  input  A,
  input  B,
  input  A_2,
  input  C,
  input  B_2,
  input  C_2,
  output Fault,
  output Fault_2,
  output Shutdown,
  output Shutdown_2
);

  wire and_1_out, and_2_out, and_3_out, and_4_out, xor_1_out, xor_2_out, xor_3_out, xor_4_out;

  and and_1 (and_1_out, A, B);
  xor xor_1 (xor_1_out, A, B);
  and and_2 (and_2_out, xor_1_out, C);
  xor xor_2 (xor_2_out, C, B);
  or or_1 (Fault, xor_1_out, xor_2_out);
  or or_2 (Shutdown, and_2_out, and_1_out);
  and and_3 (and_3_out, A_2, B_2);
  xor xor_3 (xor_3_out, A_2, B_2);
  and and_4 (and_4_out, xor_3_out, C_2);
  xor xor_4 (xor_4_out, xor_3_out, C_2);
  or or_3 (Shutdown_2, and_4_out, and_3_out);
  xor xor_5 (Fault_2, xor_4_out, Shutdown_2);

  // Notes on the sheet:
  //   Alternative
endmodule
