// Logisim project Quiz1.circ as structural Verilog: 1 circuit, main circuit main
module main (
  input  x,
  input  y,
  input  z,
  output out_4
);

  wire not_1_out, or_1_out;

  not not_1 (not_1_out, y);
  or or_1 (or_1_out, x, not_1_out);
  and and_1 (out_4, or_1_out, z);

  // Notes on the sheet:
  //   f{x,y,z) = And(Or(x,not(y)), z)
endmodule
