// Logisim project Subtraction Chip.circ as structural Verilog: 1 circuit, main circuit main
module main (
  input  a,
  input  b,
  output difference,
  output carry
);

  wire not_1_out;

  not not_1 (not_1_out, a);
  xor xor_1 (difference, a, b);
  and and_1 (carry, not_1_out, b);

  // Notes on the sheet:
  //   Quiz2 Chip: Subtraction Chip
  //   notA
endmodule
